# Fritzing sketch input (saved by Fritzing 0.9.3b)

parts:
  U1 = 74HC595 [package="DIP16 [THT]"]
  U2 = 74HC595 [package="DIP16 [THT]"]
  Part1 = Arduino Uno (Rev3) - ICSP

nets:
  GND: U1.GND, U1.OE, U2.GND, U2.OE, Part1.GND
  N1: U1.Q7', U2.DS
  VCC: U1.MR, U1.VCC, U2.MR, U2.VCC, Part1.5V
  N2: U1.SH_CP, U2.SH_CP, Part1.D7
  N3: U1.ST_CP, U2.ST_CP, Part1.D6_PWM
  N4: U1.DS, Part1.D5_PWM
