# Fritzing sketch output (saved by Fritzing 0.9.3b)

parts:
  U1 = 74HC595 [package="DIP16 [THT]"]
  U2 = 74HC595 [package="DIP16 [THT]"]
  U3 = 7-SEGMENT-4DIGIT [package=7-segment-4digit]
  R1 = Resistor [tolerance=±5% resistance=220 package="2512 [SMD]"]
  U4 = 7-SEGMENT-4DIGIT [package=7-segment-4digit]
  R2 = Resistor [tolerance=±5% resistance=220 package="2512 [SMD]"]
  R3 = Resistor [tolerance=±5% resistance=220 package="2512 [SMD]"]
  R6 = Resistor [tolerance=±5% resistance=220 package="2512 [SMD]"]
  R7 = Resistor [tolerance=±5% resistance=220 package="2512 [SMD]"]
  R8 = Resistor [tolerance=±5% resistance=220 package="2512 [SMD]"]
  R4 = Resistor [tolerance=±5% resistance=220 package="2512 [SMD]"]
  R5 = Resistor [tolerance=±5% resistance=220 package="2512 [SMD]"]

nets:
  N1: U1.Q1, R1.Pin_0
  N2: U1.Q2, R2.Pin_0
  N3: U1.Q3, R3.Pin_0
  N4: U1.Q4, R4.Pin_0
  N5: U1.Q5, R5.Pin_0
  N6: U1.Q6, R6.Pin_0
  N7: U1.Q7, R8.Pin_0
  N8: U1.Q0, R7.Pin_0
  N9: U2.Q1, U3.13, U3.14
  N10: U2.Q2, U3.11
  N11: U2.Q3, U3.9
  N12: U2.Q4, U4.15, U4.16
  N13: U2.Q5, U4.14
  N14: U2.Q6, U4.11
  N15: U2.Q7, U4.9
  N16: U2.Q0, U3.16
  N17: U3.1, U4.1, R8.Pin_1
  N18: U3.2, U4.2, R6.Pin_1
  N19: U3.3, U4.3, R5.Pin_1
  N20: U3.4, U4.4, R4.Pin_1
  N21: U3.5, U4.5, R3.Pin_1
  N22: U3.6, U4.6, R2.Pin_1
  N23: U3.7, R1.Pin_1, U4.7
  N24: U3.8, U4.8, R7.Pin_1
