# Fritzing sketch toArduinoOutput (saved by Fritzing 0.9.2b)

parts:
  Componente1 = Arduino Uno (Rev3) - ICSP
  U1 = 74HC595 [package="DIP16 [THT]"]
  U2 = 74HC595 [package="DIP16 [THT]"]

nets:
  N1: Componente1.D5_PWM, U2.DS
  N2: Componente1.D6_PWM, U1.ST_CP, U2.ST_CP
  N3: Componente1.D7, U1.SH_CP, U2.SH_CP
  N4: U1.DS, U2.Q7'
