# Fritzing sketch toArduinoVoltage (saved by Fritzing 0.9.2b)

parts:
  Componente1 = Arduino Uno (Rev3) - ICSP
  U1 = 74HC595 [package="DIP16 [THT]"]
  U2 = 74HC595 [package="DIP16 [THT]"]

nets:
  VCC: Componente1.5V, U1.MR, U1.VCC, U2.MR, U2.VCC
  GND: Componente1.GND, U1.Q7, U1.GND, U1.OE, U2.GND, U2.OE
