# Fritzing sketch toDisplay (saved by Fritzing 0.9.2b)

parts:
  U1 = 74HC595 [package="DIP16 [THT]"]
  U2 = 74HC595 [package="DIP16 [THT]"]
  R2 = Resistor [tolerance=±5% resistance=220 package="0805 [SMD]"]
  R3 = Resistor [tolerance=±5% resistance=220 package="0805 [SMD]"]
  R4 = Resistor [tolerance=±5% resistance=220 package="0805 [SMD]"]
  R5 = Resistor [tolerance=±5% resistance=220 package="0805 [SMD]"]
  R6 = Resistor [tolerance=±5% resistance=220 package="0805 [SMD]"]
  R7 = Resistor [tolerance=±5% resistance=220 package="0805 [SMD]"]
  R8 = Resistor [tolerance=±5% resistance=220 package="0805 [SMD]"]
  R9 = Resistor [tolerance=±5% resistance=220 package="0805 [SMD]"]
  U4 = 7-SEGMENT-4DIGIT [package=7-segment-4digit]

nets:
  N1: U1.Q1, U4.14
  N2: U1.Q2, U4.15
  N3: U1.Q3, U4.16
  N4: U1.Q0, U4.13
  N5: U2.Q1, R2.Pin_0
  N6: U2.Q2, R3.Pin_0
  N7: U2.Q3, R5.Pin_0
  N8: U2.Q4, R6.Pin_0
  N9: U2.Q5, R7.Pin_0
  N10: U2.Q6, R8.Pin_0
  N11: U2.Q7, R9.Pin_0
  N12: U2.Q0, R4.Pin_0
  N13: R2.Pin_1, U4.8
  N14: R3.Pin_1, U4.7
  N15: R4.Pin_1, U4.9
  N16: R5.Pin_1, U4.6
  N17: R6.Pin_1, U4.5
  N18: R7.Pin_1, U4.4
  N19: R8.Pin_1, U4.3
  N20: R9.Pin_1, U4.2
